# Fritzing sketch Circuito (saved by Fritzing 0.9.10b)
breadboards: 1

parts:
  U1 = ESP32S-HiLetgo [part_number=ESP32S-HiLetgo]
  R1 = Resistor [tolerance=±5% resistance=1k package="2512 [SMD]"]
  R2 = Resistor [tolerance=±5% resistance=220 package="2512 [SMD]"]
  R3 = Photocell (LDR) [package=THT]
  LED1 = smd LED [color="Red (633nm)" package="0603 [SMD]"]

nets:
  N1: U1.3.3, R3.pin_1
  N2: U1.GND, R2.Pin_0, LED1.cathode
  N3: U1.GPIO15, R2.Pin_1, R3.pin_0
  N4: U1.GPIO23, R1.Pin_0
  N5: R1.Pin_1, LED1.anode

notes:
  Fios:
  - Vermelho = 3v3
  - Azuis = GND
  - Amarelo = Porta 23 do ESP32
  - Verde = Porta 15 do ESP32

custom parts:
  ESP32S-HiLetgo: HiLetgo ESP-WROOM-32 ESP32 ESP-32S Development Board 2.4GHz Dual-Mode WiFi + Bluetooth Dual Cores Microcontroller The ESP32 integrated with Antenna switches, RF Balun, power amplifiers, low-noise amplifiers, filters, and management modules, and the entire solution occupies the least area of PCB. 2.4 GHz Wi-Fi plus Bluetooth dual-mode chip, with TSMC Ultra-low power consumption 40nm technology,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
